# Fritzing sketch programmer_reminder (saved by Fritzing 0.9.4)
breadboards: 1

parts:
  Part1 = Arduino Uno (Rev3)
  M1 = BME280
  Part2 = BH1750
  OLED1 = OLED 128x64 I2C Monochrome Display
  Piezo1 = Piezo Speaker - PC Mount [part_number=COM-07950]
  S1 = Pushbutton [package="[THT]"]
  S2 = Pushbutton [package="[THT]"]
  S3 = Pushbutton [package="[THT]"]
  R6 = Resistor [tolerance=±5% resistance=10k package="1206 [SMD]"]
  R7 = Resistor [tolerance=±5% resistance=10k package="1206 [SMD]"]
  R8 = Resistor [tolerance=±5% resistance=10k package="1206 [SMD]"]
  R9 = Resistor [tolerance=±5% resistance=100 package="0402 [SMD]"]

nets:
  N1: Part1.A4/SDA, M1.SDA, Part2.SDA, OLED1.SDA
  N2: Part1.A5/SCL, M1.SCL, Part2.SCL, OLED1.SCK
  N3: Part1.D8, R9.Pin_1
  N4: Part1.D5_PWM, S1.Pin_1, S1.Pin_2, R6.Pin_0
  N5: Part1.D6_PWM, S2.Pin_1, S2.Pin_2, R7.Pin_0
  N6: Part1.D7, S3.Pin_1, S3.Pin_2, R8.Pin_0
  5V: Part1.5V, M1.VIN, Part2.VCC, OLED1.VDD, S1.Pin_3, S1.Pin_4, S2.Pin_3, S2.Pin_4, S3.Pin_3, S3.Pin_4
  GND: Part1.GND, M1.GND, Part2.GND, OLED1.GND, Piezo1.GND, R6.Pin_1, R7.Pin_1, R8.Pin_1
  N7: Piezo1.VCC, R9.Pin_0

custom parts:
  BME280: Temperature Humidity Barometric presure Sensor
  BH1750: Light Sensor
  Piezo Speaker - PC Mount: This is a small 12mm round speaker that operates around the audible 2kHz range. You can use these speakers to create simple music or user interfaces. Each speaker is PTH solderable and requires an operating voltage of 3.5-5V with a mean current of 35mA max. These speakers also have a typical sound output of 95 dBA and a coil resistance of 42 ±6.3 ohms.
